// Logisim project Addition Function.circ as structural Verilog: 2 circuits, main circuit main
module main (
  input  Subber,
  input  I0,
  input  I1,
  input  I2,
  input  J0,
  input  J1,
  input  J2,
  output S0,
  output S1,
  output S2,
  output S3
);

  wire and_1_out, and_2_out, and_3_out, and_4_out, and_5_out, and_7_out, and_8_out, not_1_out, not_2_out,
       not_3_out, not_4_out, not_5_out, or_1_out, or_3_out, or_4_out, or_5_out, or_6_out, or_7_out;

  and and_1 (and_1_out, I0, J0);
  and and_2 (and_2_out, or_4_out, I2);
  not not_1 (not_1_out, and_1_out);
  or or_1 (or_1_out, and_1_out, I1);
  and and_3 (and_3_out, and_1_out, I1);
  or or_2 (S3, and_2_out, and_8_out);
  or or_3 (or_3_out, I0, J0);
  and and_4 (and_4_out, or_1_out, not_2_out);
  not not_2 (not_2_out, and_3_out);
  or or_4 (or_4_out, and_7_out, and_3_out);
  and and_5 (and_5_out, or_6_out, not_3_out);
  not not_3 (not_3_out, and_2_out);
  and and_6 (S0, not_1_out, or_3_out);
  or or_5 (or_5_out, and_4_out, J1);
  not not_4 (not_4_out, and_7_out);
  and and_7 (and_7_out, and_4_out, J1);
  or or_6 (or_6_out, or_4_out, I2);
  or or_7 (or_7_out, and_5_out, J2);
  not not_5 (not_5_out, and_8_out);
  and and_8 (and_8_out, and_5_out, J2);
  and and_9 (S1, or_5_out, not_4_out);
  and and_10 (S2, or_7_out, not_5_out);
endmodule

module Full_Adder (
  input  Carry,
  input  I0,
  input  J0,
  output S0,
  output Carry_2
);

  // AND_Gate and_1 is placed but not wired
endmodule
